// Digital circuit labtimer.dig as structural Verilog
module labtimer (
  input  CLK,
  input  SW,
  input  B3,
  input  B2,
  input  B1,
  input  B0,
  input  HZ1,
  output [3:0] M10,
  output [3:0] M1,
  output [3:0] S10,
  output [3:0] S1
);

  wire and_1_out, and_2_out, and_3_out, and_4_out, and_5_out, and_6_out, and_7_out, and_8_out, and_9_out,
       and_10_out, and_11_out, and_12_out, and_13_out, and_14_out, and_15_out, and_16_out, and_17_out,
       and_18_out, and_19_out, and_20_out, and_21_out, and_22_out, and_23_out, and_24_out, and_25_out,
       comparator_1_eq, comparator_2_eq, comparator_3_eq, comparator_4_eq, comparator_5_eq, comparator_6_eq,
       comparator_7_eq, comparator_8_eq, comparator_9_eq, comparator_10_eq, comparator_11_eq,
       comparator_12_eq, count_dir_q, d_ff_1_q, d_ff_2_q, d_ff_3_q, d_ff_4_q, d_ff_5_q, d_ff_6_q, d_ff_7_q,
       d_ff_8_q, not_1_out, not_2_out, not_3_out, not_4_out, not_5_out, not_6_out, not_7_out, not_8_out,
       not_9_out, not_10_out, not_11_out, not_12_out, not_13_out, not_14_out, or_1_out, or_2_out, or_3_out,
       or_4_out, or_5_out, or_6_out, or_7_out, or_8_out, Zero_Detect_2_eq, Zero_Detect_3_eq,
       Zero_Detect_4_eq, Zero_Detect_eq;
  wire [3:0] add_1_s, add_2_s, add_3_s, add_4_s, add_5_s, add_6_s, add_7_s, add_8_s, multiplexer_1_out,
       multiplexer_2_out, multiplexer_3_out, multiplexer_4_out, multiplexer_5_out, multiplexer_6_out,
       multiplexer_7_out, multiplexer_8_out, multiplexer_9_out, multiplexer_10_out, multiplexer_11_out,
       multiplexer_12_out, multiplexer_13_out, multiplexer_14_out, multiplexer_15_out, multiplexer_16_out,
       multiplexer_17_out, multiplexer_18_out, multiplexer_19_out, multiplexer_20_out, sub_1_s, sub_2_s,
       sub_3_s, sub_4_s;

  D_FF d_ff_1 (.D(HZ1), .C(CLK), .Q(d_ff_1_q));  // open: nQ
  not not_1 (not_1_out, d_ff_1_q);
  and and_1 (and_1_out, not_1_out, HZ1);
  not not_2 (not_2_out, SW);
  and and_2 (and_2_out, not_2_out, and_1_out);
  D_FF d_ff_2 (.D(B3), .C(CLK), .Q(d_ff_2_q));  // open: nQ
  D_FF d_ff_3 (.D(B2), .C(CLK), .Q(d_ff_3_q));  // open: nQ
  D_FF d_ff_4 (.D(B1), .C(CLK), .Q(d_ff_4_q));  // open: nQ
  D_FF d_ff_5 (.D(B0), .C(CLK), .Q(d_ff_5_q));  // open: nQ
  not not_3 (not_3_out, d_ff_2_q);
  not not_4 (not_4_out, d_ff_3_q);
  not not_5 (not_5_out, d_ff_4_q);
  not not_6 (not_6_out, d_ff_5_q);
  and and_3 (and_3_out, not_3_out, B3);
  and and_4 (and_4_out, not_4_out, B2);
  and and_5 (and_5_out, not_5_out, B1);
  and and_6 (and_6_out, not_6_out, B0);
  and and_7 (and_7_out, and_4_out, SW);
  and and_8 (and_8_out, and_5_out, SW);
  and and_9 (and_9_out, and_6_out, SW);
  Multiplexer #(.Bits(4)) multiplexer_1 (
    .sel(SW), .in_0(multiplexer_17_out), .in_1(multiplexer_5_out), .out(multiplexer_1_out));
  Multiplexer #(.Bits(4)) multiplexer_2 (
    .sel(SW), .in_0(multiplexer_18_out), .in_1(multiplexer_6_out), .out(multiplexer_2_out));
  Multiplexer #(.Bits(4)) multiplexer_3 (
    .sel(SW), .in_0(multiplexer_19_out), .in_1(multiplexer_7_out), .out(multiplexer_3_out));
  Multiplexer #(.Bits(4)) multiplexer_4 (
    .sel(SW), .in_0(multiplexer_20_out), .in_1(multiplexer_8_out), .out(multiplexer_4_out));
  and and_10 (and_10_out, not_2_out, or_8_out);
  and and_11 (and_11_out, not_2_out, or_8_out, or_7_out);
  and and_12 (and_12_out, not_2_out, or_8_out, or_6_out, or_7_out);
  Comparator #(.Bits(4)) Zero_Detect (.a(M10), .b(4'b0000), .eq(Zero_Detect_eq));  // open: gt, lt
  Comparator #(.Bits(4)) Zero_Detect_2 (.a(M1), .b(4'b0000), .eq(Zero_Detect_2_eq));  // open: gt, lt
  Comparator #(.Bits(4)) Zero_Detect_3 (.a(S10), .b(4'b0000), .eq(Zero_Detect_3_eq));  // open: gt, lt
  Comparator #(.Bits(4)) Zero_Detect_4 (.a(S1), .b(4'b0000), .eq(Zero_Detect_4_eq));  // open: gt, lt
  and and_13 (and_13_out, SW, and_3_out);
  or or_1 (or_1_out, and_13_out, and_19_out);
  or or_2 (or_2_out, and_7_out, and_18_out);
  or or_3 (or_3_out, and_8_out, and_15_out);
  or or_4 (or_4_out, and_9_out, and_2_out);
  D_FF d_ff_6 (.D(and_10_out), .C(CLK), .Q(d_ff_6_q));  // open: nQ
  Register #(.Bits(4)) register_1 (.D(multiplexer_1_out), .C(CLK), .en(or_1_out), .Q(M10));
  Register #(.Bits(4)) register_2 (.D(multiplexer_2_out), .C(CLK), .en(or_2_out), .Q(M1));
  Register #(.Bits(4)) register_3 (.D(multiplexer_3_out), .C(CLK), .en(or_3_out), .Q(S10));
  Register #(.Bits(4)) register_4 (.D(multiplexer_4_out), .C(CLK), .en(or_4_out), .Q(S1));
  not not_7 (not_7_out, d_ff_6_q);
  and and_14 (and_14_out, Zero_Detect_eq, Zero_Detect_2_eq, Zero_Detect_3_eq, Zero_Detect_4_eq);
  and and_15 (and_15_out, not_7_out, and_10_out);
  not not_8 (not_8_out, SW);
  Add #(.Bits(4)) add_1 (.a(M10), .b(4'b0001), .c_i(1'b0), .s(add_1_s));  // open: c_o
  Comparator #(.Bits(4)) comparator_1 (.a(M10), .b(4'b1001), .eq(comparator_1_eq));  // open: gt, lt
  Add #(.Bits(4)) add_2 (.a(M1), .b(4'b0001), .c_i(1'b0), .s(add_2_s));  // open: c_o
  Comparator #(.Bits(4)) comparator_2 (.a(M1), .b(4'b1001), .eq(comparator_2_eq));  // open: gt, lt
  Add #(.Bits(4)) add_3 (.a(S10), .b(4'b0001), .c_i(1'b0), .s(add_3_s));  // open: c_o
  Comparator #(.Bits(4)) comparator_3 (.a(S10), .b(4'b0101), .eq(comparator_3_eq));  // open: gt, lt
  Add #(.Bits(4)) add_4 (.a(S1), .b(4'b0001), .c_i(1'b0), .s(add_4_s));  // open: c_o
  Comparator #(.Bits(4)) comparator_4 (.a(S1), .b(4'b1001), .eq(comparator_4_eq));  // open: gt, lt
  D_FF d_ff_7 (.D(and_11_out), .C(CLK), .Q(d_ff_7_q));  // open: nQ
  D_FF d_ff_8 (.D(and_12_out), .C(CLK), .Q(d_ff_8_q));  // open: nQ
  and and_16 (and_16_out, and_14_out, not_11_out);
  and and_17 (and_17_out, count_dir_q, not_8_out);
  not not_9 (not_9_out, d_ff_7_q);
  not not_10 (not_10_out, d_ff_8_q);
  Multiplexer #(.Bits(4)) multiplexer_5 (
    .sel(comparator_1_eq), .in_0(add_1_s), .in_1(4'b0000), .out(multiplexer_5_out));
  Multiplexer #(.Bits(4)) multiplexer_6 (
    .sel(comparator_2_eq), .in_0(add_2_s), .in_1(4'b0000), .out(multiplexer_6_out));
  Multiplexer #(.Bits(4)) multiplexer_7 (
    .sel(comparator_3_eq), .in_0(add_3_s), .in_1(4'b0000), .out(multiplexer_7_out));
  Multiplexer #(.Bits(4)) multiplexer_8 (
    .sel(comparator_4_eq), .in_0(add_4_s), .in_1(4'b0000), .out(multiplexer_8_out));
  and and_18 (and_18_out, not_9_out, and_11_out);
  and and_19 (and_19_out, not_10_out, and_12_out);
  or or_5 (or_5_out, and_16_out, and_17_out);
  Register count_dir (.D(or_5_out), .C(CLK), .en(not_8_out), .Q(count_dir_q));
  not not_11 (not_11_out, count_dir_q);
  Add #(.Bits(4)) add_5 (.a(M10), .b(4'b0001), .c_i(1'b0), .s(add_5_s));  // open: c_o
  Sub #(.Bits(4)) sub_1 (.a(M10), .b(4'b0001), .c_i(1'b0), .s(sub_1_s));  // open: c_o
  Add #(.Bits(4)) add_6 (.a(M1), .b(4'b0001), .c_i(1'b0), .s(add_6_s));  // open: c_o
  Sub #(.Bits(4)) sub_2 (.a(M1), .b(4'b0001), .c_i(1'b0), .s(sub_2_s));  // open: c_o
  Add #(.Bits(4)) add_7 (.a(S10), .b(4'b0001), .c_i(1'b0), .s(add_7_s));  // open: c_o
  Sub #(.Bits(4)) sub_3 (.a(S10), .b(4'b0001), .c_i(1'b0), .s(sub_3_s));  // open: c_o
  Add #(.Bits(4)) add_8 (.a(S1), .b(4'b0001), .c_i(1'b0), .s(add_8_s));  // open: c_o
  Sub #(.Bits(4)) sub_4 (.a(S1), .b(4'b0001), .c_i(1'b0), .s(sub_4_s));  // open: c_o
  Comparator #(.Bits(4)) comparator_5 (.a(M10), .b(4'b1001), .eq(comparator_5_eq));  // open: gt, lt
  Comparator #(.Bits(4)) comparator_6 (.a(M10), .b(4'b0000), .eq(comparator_6_eq));  // open: gt, lt
  Comparator #(.Bits(4)) comparator_7 (.a(M1), .b(4'b1001), .eq(comparator_7_eq));  // open: gt, lt
  Comparator #(.Bits(4)) comparator_8 (.a(M1), .b(4'b0000), .eq(comparator_8_eq));  // open: gt, lt
  Comparator #(.Bits(4)) comparator_9 (.a(S10), .b(4'b0101), .eq(comparator_9_eq));  // open: gt, lt
  Comparator #(.Bits(4)) comparator_10 (.a(S10), .b(4'b0000), .eq(comparator_10_eq));  // open: gt, lt
  Comparator #(.Bits(4)) comparator_11 (.a(S1), .b(4'b1001), .eq(comparator_11_eq));  // open: gt, lt
  Comparator #(.Bits(4)) comparator_12 (.a(S1), .b(4'b0000), .eq(comparator_12_eq));  // open: gt, lt
  Multiplexer #(.Bits(4)) multiplexer_9 (
    .sel(comparator_6_eq), .in_0(sub_1_s), .in_1(4'b1001), .out(multiplexer_9_out));
  Multiplexer #(.Bits(4)) multiplexer_10 (
    .sel(comparator_8_eq), .in_0(sub_2_s), .in_1(4'b1001), .out(multiplexer_10_out));
  Multiplexer #(.Bits(4)) multiplexer_11 (
    .sel(comparator_10_eq), .in_0(sub_3_s), .in_1(4'b0101), .out(multiplexer_11_out));
  Multiplexer #(.Bits(4)) multiplexer_12 (
    .sel(comparator_12_eq), .in_0(sub_4_s), .in_1(4'b1001), .out(multiplexer_12_out));
  Multiplexer #(.Bits(4)) multiplexer_13 (
    .sel(comparator_5_eq), .in_0(add_5_s), .in_1(4'b0000), .out(multiplexer_13_out));
  Multiplexer #(.Bits(4)) multiplexer_14 (
    .sel(comparator_7_eq), .in_0(add_6_s), .in_1(4'b0000), .out(multiplexer_14_out));
  Multiplexer #(.Bits(4)) multiplexer_15 (
    .sel(comparator_9_eq), .in_0(add_7_s), .in_1(4'b0000), .out(multiplexer_15_out));
  Multiplexer #(.Bits(4)) multiplexer_16 (
    .sel(comparator_11_eq), .in_0(add_8_s), .in_1(4'b0000), .out(multiplexer_16_out));
  Multiplexer #(.Bits(4)) multiplexer_17 (
    .sel(count_dir_q), .in_0(multiplexer_9_out), .in_1(multiplexer_13_out), .out(multiplexer_17_out));
  Multiplexer #(.Bits(4)) multiplexer_18 (
    .sel(count_dir_q), .in_0(multiplexer_10_out), .in_1(multiplexer_14_out), .out(multiplexer_18_out));
  Multiplexer #(.Bits(4)) multiplexer_19 (
    .sel(count_dir_q), .in_0(multiplexer_11_out), .in_1(multiplexer_15_out), .out(multiplexer_19_out));
  Multiplexer #(.Bits(4)) multiplexer_20 (
    .sel(count_dir_q), .in_0(multiplexer_12_out), .in_1(multiplexer_16_out), .out(multiplexer_20_out));
  not not_12 (not_12_out, count_dir_q);
  not not_13 (not_13_out, count_dir_q);
  not not_14 (not_14_out, count_dir_q);
  and and_20 (and_20_out, comparator_7_eq, count_dir_q, count_dir_q);
  and and_21 (and_21_out, comparator_8_eq, and_1_out, not_13_out);
  and and_22 (and_22_out, comparator_9_eq, and_1_out, count_dir_q);
  and and_23 (and_23_out, comparator_10_eq, and_1_out, not_14_out);
  and and_24 (and_24_out, comparator_11_eq, and_1_out, count_dir_q);
  and and_25 (and_25_out, comparator_12_eq, and_1_out, not_12_out);
  or or_6 (or_6_out, and_20_out, and_21_out);
  or or_7 (or_7_out, and_22_out, and_23_out);
  or or_8 (or_8_out, and_24_out, and_25_out);

  // Notes on the sheet:
  //   SW: default 1
endmodule
